# Fritzing sketch KBS-KinderBenachrichtigungsSystem (saved by Fritzing 0.9.3b)

parts:
  16x2_LCD_Displaymit_I2C = LCD1602-I2C
  Raspberry_Pi_Zero = Raspberry Pi Zero
  BIOS_Buzzer = Piezo Speaker

nets:
  N1: 16x2_LCD_Displaymit_I2C.GND, Raspberry_Pi_Zero.pin_6, Raspberry_Pi_Zero.pin_9, BIOS_Buzzer.pin1
  N2: 16x2_LCD_Displaymit_I2C.VCC, Raspberry_Pi_Zero.pin_2
  N3: 16x2_LCD_Displaymit_I2C.SDA, Raspberry_Pi_Zero.pin_3
  N4: 16x2_LCD_Displaymit_I2C.SCL, Raspberry_Pi_Zero.pin_5
  N5: Raspberry_Pi_Zero.pin_10, BIOS_Buzzer.pin2

custom parts:
  LCD1602-I2C: A standard character display, usually with 2x16 characters. Comes in many colors with LCM1602 IIC attached.
